# Fritzing sketch BolightSchematic (saved by Fritzing 0.9.3b)

parts:
  U1 = NodeMCU V3.0
  R1 = Resistor [tolerance=±5% resistance=220 package=THT]
  S1 = Momentary Switch [package=ksa_sealed_tac_switch]

nets:
  N1: U1.D7, R1.Pin_0, S1.2
  N2: U1.GND, R1.Pin_1
  N3: U1.Vin, S1.3

custom parts:
  NodeMCU V3.0: ESP8266 based NodeMCU
